# Fritzing sketch schema_cablage_robot (saved by Fritzing 0.9.5d)

parts:
  L298N1 = L298N DC motor driver
  Part1 = Arduino Uno (Rev3)
  U2 = LIPO-2000mAh [package=lipo-2000]  # not connected
  M1 = DC Motor  # not connected
  M2 = DC Motor  # not connected
  M4 = Dagu DGServo 9g (End View) [part_number=RS001B]
  HC-SR04_Sensor_1 = HC-SR04 Ultrasonic Distance Sensor

nets:
  5V: L298N1.5V, Part1.VIN
  N1: L298N1.ENA, Part1.D3_PWM
  N2: L298N1.ENB, Part1.D11_PWM/MOSI
  N3: L298N1.IN1, Part1.D5_PWM
  N4: L298N1.IN2, Part1.D6_PWM
  N5: L298N1.IN3, Part1.D9_PWM
  N6: L298N1.IN4, Part1.D10_PWM/SS
  N7: Part1.A3, M4.pulse
  N8: Part1.D8, HC-SR04_Sensor_1.ECHO
  N9: Part1.AREF, HC-SR04_Sensor_1.GND
  N10: Part1.D7, HC-SR04_Sensor_1.TRIG
  3V3: Part1.3V3, M4.vcc
  5V_2: Part1.5V, HC-SR04_Sensor_1.VCC
  GND: Part1.GND, M4.gnd

notes:
  Left Motor
  Right Motor
  L298N Motor Driver Board
  2 x 3.7 V Batteries
  HC-SR04 Sensor UltraSound
  Servo-motor Sensor
  Arduino UNO

custom parts:
  L298N DC motor driver: 2x DC motor driver with 78M05 positive voltage regulator (7..35 V) L298N: max 46 V, 2 A Set 5 V Enable jumper to enable 5 V regultor (needed for the L298N) and +5 V output at screw terminal or supply external +5 V at screw terminal Set ENA and/or ENB to +5 V to enable motor permanently or supply ENA and/or ENB with PWM signal IN1 and IN2 set rotation directory for motor A (OUT1/OUT2) IN2 and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
